# Fritzing sketch Sketch Arduino JWS + DHT22 (saved by Fritzing 0.9.3b)

parts:
  Part1 = Arduino Uno (Rev3)
  U1 = LCD-16X2 [package=lcd-16x2_noholes]
  Part2 = Adafruit DS1307 RTC Breakout [part_number="Adafruit #264"]
  DHT1 = DHT22 Humidity and Temperature Sensor
  LCM1602_IIC1 = LCM1602 IIC [part_number="LCM1602 IIC" chip_label="LCM1602 IIC" package="DIP (Dual Inline) [THT]"]
  R1 = Resistor [tolerance=±5% resistance=10k package=THT]

nets:
  N1: Part1.A4/SDA, Part2.SDA, LCM1602_IIC1.SDA
  N2: Part1.A5/SCL, Part2.SCL, LCM1602_IIC1.SCL
  N3: Part1.D2, DHT1.DATA, R1.Pin_0
  VCC: Part1.5V, Part2.VCC, LCM1602_IIC1.VCC, R1.Pin_1
  GND: Part1.GND, Part2.GND, DHT1.GND, LCM1602_IIC1.GND
  VSS: U1.VSS, LCM1602_IIC1.VSS
  VDD: U1.VDD, LCM1602_IIC1.VDD
  N4: U1.VO, LCM1602_IIC1.V0
  N5: U1.RS, LCM1602_IIC1.RS
  N6: U1.R_W, LCM1602_IIC1.RW
  N7: U1.E, LCM1602_IIC1.E
  N8: U1.DB0, LCM1602_IIC1.D0
  N9: U1.DB1, LCM1602_IIC1.D1
  N10: U1.DB2, LCM1602_IIC1.D2
  N11: U1.DB3, LCM1602_IIC1.D3
  N12: U1.DB4, LCM1602_IIC1.D4
  N13: U1.DB5, LCM1602_IIC1.D5
  N14: U1.DB6, LCM1602_IIC1.D6
  N15: U1.DB7, LCM1602_IIC1.D7
  N16: U1.A, LCM1602_IIC1.A
  N17: U1.K, LCM1602_IIC1.K
  N18: LCM1602_IIC1.LED_A, LCM1602_IIC1.LED_B

custom parts:
  Adafruit DS1307 RTC Breakout: This is a great battery-backed real time clock (RTC) that allows your microcontroller project to keep track of time even if it is reprogrammed, or if the power is lost. Perfect for datalogging, clock-building, time stamping, timers and alarms, etc. The DS1307 is the most popular RTC - but it requires 5V power to work (although we've used it with 5V power and 3.3V logic successfully) PCB &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
  LCM1602 IIC: I2C-Module to use a 1602 or 2004 LCD on with the wire.h libory Serial LCD Modul
